// Logisim project ax8.circ as structural Verilog: 28 circuits, main circuit full_adder
module main (
);

  wire alu_1_c, alu_1_halt, alu_1_n, alu_1_v, alu_1_z, Cin_p1, Vin_p1;
  wire [3:0] undriven_3;
  wire [7:0] alu_1_y, undriven, undriven_2;

  // DipSwitch A: pin names not known
  // DipSwitch B: pin names not known
  // DipSwitch #(.number(4)) OP: pin names not known
  alu alu_1 (
    .A(undriven), .B(undriven_2), .Cin(Cin_p1), .Vin(Vin_p1), .OP(undriven_3), .Y(alu_1_y), .C(alu_1_c),
    .V(alu_1_v), .Z(alu_1_z), .N(alu_1_n), .HALT(alu_1_halt));
  // DipSwitch #(.number(1)) Cin: pin names not known; wires that end beside it: Cin_p1
  // DipSwitch #(.number(1)) Vin: pin names not known; wires that end beside it: Vin_p1
  Hex_Digit_Display hex_digit_display_1 (.value(alu_1_y[7:4]));  // open: dp
  Hex_Digit_Display hex_digit_display_2 (.value(alu_1_y[3:0]));  // open: dp
  LedBar #(.matrixcols(4)) ZNCV (.led0(alu_1_z), .led1(alu_1_n), .led2(alu_1_c), .led3(alu_1_v));
  LED HLT (.in(alu_1_halt));

  // Notes on the sheet:
  //   OP: 0000 => ADC
  //   0001 => SBC
  //   0010 => MUL
  //   0011 => AND
  //   0100 => OR
  //   0101 => XOR
  //   0110 => ROL
  //   0111 => ROR
  //   1000 => MOV
  //   1xxx => HLT
endmodule

module d_latch (
  input  D,
  input  CLK,
  output Q,
  output NQ
);

  wire buffer_1_out, buffer_2_out, buffer_3_out, nand_1_out, nand_2_out, not_1_out;

  not not_1 (not_1_out, D);
  nand nand_1 (nand_1_out, D, CLK);
  nand nand_2 (nand_2_out, CLK, not_1_out);
  buf buffer_1 (buffer_1_out, buffer_2_out);
  buf buffer_2 (buffer_2_out, buffer_3_out);
  nand nand_3 (Q, NQ, nand_1_out);
  nand nand_4 (NQ, nand_2_out, buffer_1_out);
  buf buffer_3 (buffer_3_out, Q);

  // Notes on the sheet:
  //   Logisim is BUGGY, So I can't use this implementation
endmodule

module d_flipflop (
  input  D,
  input  CLK,
  output Q,
  output NQ
);

  wire d_ff_1_q, not_1_out;

  D_Flip_Flop d_ff_1 (.D(D), .clk(not_1_out), .Q(d_ff_1_q));  // open: Qn, preset, reset
  not not_1 (not_1_out, CLK);
  D_Flip_Flop d_ff_2 (.D(d_ff_1_q), .clk(CLK), .Q(Q), .Qn(NQ));  // open: preset, reset

  // Notes on the sheet:
  //   Rising edge D-FlipFlop
endmodule

module mux_2to1 (
  input  S,
  input  IN0,
  input  IN1,
  output Y
);

  wire nand_1_out, nand_3_out, not_1_out;

  not not_1 (not_1_out, S);
  nand nand_1 (nand_1_out, not_1_out, IN0);
  nand nand_2 (Y, nand_1_out, nand_3_out);
  nand nand_3 (nand_3_out, IN1, S);
endmodule

module mux_2to1_4 (
  input  S,
  input  [3:0] IN0,
  input  [3:0] IN1,
  output [3:0] Y
);

  mux_2to1 mux_2to1_1 (.IN0(IN0[0]), .IN1(IN1[0]), .S(S), .Y(Y[0]));
  mux_2to1 mux_2to1_2 (.IN0(IN0[1]), .IN1(IN1[1]), .S(S), .Y(Y[1]));
  mux_2to1 mux_2to1_3 (.IN0(IN0[2]), .IN1(IN1[2]), .S(S), .Y(Y[2]));
  mux_2to1 mux_2to1_4 (.IN0(IN0[3]), .IN1(IN1[3]), .S(S), .Y(Y[3]));
endmodule

module mux_2to1_8 (
  input  S,
  input  [7:0] IN0,
  input  [7:0] IN1,
  output [7:0] Y
);

  mux_2to1_4 mux_2to1_4_1 (.S(S), .IN0(IN0[3:0]), .IN1(IN1[3:0]), .Y(Y[3:0]));
  mux_2to1_4 mux_2to1_4_2 (.S(S), .IN0(IN0[7:4]), .IN1(IN1[7:4]), .Y(Y[7:4]));
endmodule

module mux_4to1 (
  input  I0,
  input  I1,
  input  I2,
  input  I3,
  input  [1:0] S,
  output Y
);

  wire mux_2to1_1_y, mux_2to1_3_y;

  mux_2to1 mux_2to1_1 (.IN0(I0), .IN1(I1), .S(S[0]), .Y(mux_2to1_1_y));
  mux_2to1 mux_2to1_2 (.IN0(mux_2to1_1_y), .IN1(mux_2to1_3_y), .S(S[1]), .Y(Y));
  mux_2to1 mux_2to1_3 (.IN0(I2), .IN1(I3), .S(S[0]), .Y(mux_2to1_3_y));
endmodule

module mux_4to1_4 (
  input  [1:0] S,
  input  [3:0] IN0,
  input  [3:0] IN1,
  input  [3:0] IN2,
  input  [3:0] IN3,
  output [3:0] Y
);

  mux_4to1 mux_4to1_1 (.I0(IN0[0]), .I1(IN1[0]), .I2(IN2[0]), .I3(IN3[0]), .S(S), .Y(Y[0]));
  mux_4to1 mux_4to1_2 (.I0(IN0[1]), .I1(IN1[1]), .I2(IN2[1]), .I3(IN3[1]), .S(S), .Y(Y[1]));
  mux_4to1 mux_4to1_3 (.I0(IN0[2]), .I1(IN1[2]), .I2(IN2[2]), .I3(IN3[2]), .S(S), .Y(Y[2]));
  mux_4to1 mux_4to1_4 (.I0(IN0[3]), .I1(IN1[3]), .I2(IN2[3]), .I3(IN3[3]), .S(S), .Y(Y[3]));
endmodule

module mux_8to1 (
  input  [2:0] S,
  input  I0,
  input  I1,
  input  I2,
  input  I3,
  input  I4,
  input  I5,
  input  I6,
  input  I7,
  output out_10
);

  wire mux_4to1_1_y, mux_4to1_2_y;

  mux_4to1 mux_4to1_1 (.I0(I0), .I1(I1), .I2(I2), .I3(I3), .S(S[1:0]), .Y(mux_4to1_1_y));
  mux_2to1 mux_2to1_1 (.IN0(mux_4to1_1_y), .IN1(mux_4to1_2_y), .S(S[2]), .Y(out_10));
  mux_4to1 mux_4to1_2 (.I0(I4), .I1(I5), .I2(I6), .I3(I7), .S(S[1:0]), .Y(mux_4to1_2_y));
endmodule

module mux_8to1_8 (
  input  [7:0] IN7,
  input  [7:0] IN6,
  input  [7:0] IN5,
  input  [7:0] IN4,
  input  [7:0] IN3,
  input  [7:0] IN2,
  input  [7:0] IN1,
  input  [7:0] IN0,
  input  [2:0] S,
  output [7:0] out_10
);

  wire [3:0] mux_4to1_4_1_y, mux_4to1_4_2_y, mux_4to1_4_3_y, mux_4to1_4_4_y;

  mux_4to1_4 mux_4to1_4_1 (
    .S(S[1:0]), .IN0(IN0[3:0]), .IN1(IN1[3:0]), .IN2(IN2[3:0]), .IN3(IN3[3:0]), .Y(mux_4to1_4_1_y));
  mux_4to1_4 mux_4to1_4_2 (
    .S(S[1:0]), .IN0(IN4[3:0]), .IN1(IN5[3:0]), .IN2(IN6[3:0]), .IN3(IN7[3:0]), .Y(mux_4to1_4_2_y));
  mux_4to1_4 mux_4to1_4_3 (
    .S(S[1:0]), .IN0(IN0[7:4]), .IN1(IN1[7:4]), .IN2(IN2[7:4]), .IN3(IN3[7:4]), .Y(mux_4to1_4_3_y));
  mux_4to1_4 mux_4to1_4_4 (
    .S(S[1:0]), .IN0(IN4[7:4]), .IN1(IN5[7:4]), .IN2(IN6[7:4]), .IN3(IN7[7:4]), .Y(mux_4to1_4_4_y));
  mux_2to1_4 mux_2to1_4_1 (.S(S[2]), .IN0(mux_4to1_4_1_y), .IN1(mux_4to1_4_2_y), .Y(out_10[3:0]));
  mux_2to1_4 mux_2to1_4_2 (.S(S[2]), .IN0(mux_4to1_4_3_y), .IN1(mux_4to1_4_4_y), .Y(out_10[7:4]));
endmodule

module demux_2to1 (
  input  S,
  input  I,
  output Y0,
  output Y1
);

  wire not_1_out;

  not not_1 (not_1_out, S);
  and and_1 (Y0, not_1_out, I);
  and and_2 (Y1, S, I);
endmodule

module demux_4to1 (
  input  I,
  input  [1:0] S,
  output Y0,
  output Y1,
  output Y2,
  output Y3
);

  wire demux_2to1_1_y0, demux_2to1_1_y1;

  demux_2to1 demux_2to1_1 (.S(S[1]), .I(I), .Y0(demux_2to1_1_y0), .Y1(demux_2to1_1_y1));
  demux_2to1 demux_2to1_2 (.S(S[0]), .I(demux_2to1_1_y0), .Y0(Y0), .Y1(Y1));
  demux_2to1 demux_2to1_3 (.S(S[0]), .I(demux_2to1_1_y1), .Y0(Y2), .Y1(Y3));
endmodule

module demux_8to1 (
  input  I,
  input  [2:0] S,
  output Y0,
  output Y1,
  output Y2,
  output Y3,
  output Y4,
  output Y5,
  output Y6,
  output Y7
);

  wire demux_2to1_1_y0, demux_2to1_1_y1;

  demux_2to1 demux_2to1_1 (.S(S[2]), .I(I), .Y0(demux_2to1_1_y0), .Y1(demux_2to1_1_y1));
  demux_4to1 demux_4to1_1 (.I(demux_2to1_1_y0), .S(S[1:0]), .Y0(Y0), .Y1(Y1), .Y2(Y2), .Y3(Y3));
  demux_4to1 demux_4to1_2 (.I(demux_2to1_1_y1), .S(S[1:0]), .Y0(Y4), .Y1(Y5), .Y2(Y6), .Y3(Y7));
endmodule

module full_adder (
  input  A,
  input  B,
  input  Cin,
  output Y,
  output Cout
);

  wire and_1_out, and_2_out, xor_1_out;

  xor xor_1 (xor_1_out, A, B);
  and and_1 (and_1_out, xor_1_out, Cin);
  and and_2 (and_2_out, A, B);
  xor xor_2 (Y, xor_1_out, Cin);
  or or_1 (Cout, and_1_out, and_2_out);
endmodule

module ripple_adder_4 (
  input  [3:0] A,
  input  [3:0] B,
  input  Cin,
  output [3:0] Y,
  output Cout
);

  wire full_adder_1_cout, full_adder_2_cout, full_adder_3_cout;

  full_adder full_adder_1 (.A(A[0]), .B(B[0]), .Cin(Cin), .Y(Y[0]), .Cout(full_adder_1_cout));
  full_adder full_adder_2 (.A(A[1]), .B(B[1]), .Cin(full_adder_1_cout), .Y(Y[1]), .Cout(full_adder_2_cout));
  full_adder full_adder_3 (.A(A[2]), .B(B[2]), .Cin(full_adder_2_cout), .Y(Y[2]), .Cout(full_adder_3_cout));
  full_adder full_adder_4 (.A(A[3]), .B(B[3]), .Cin(full_adder_3_cout), .Y(Y[3]), .Cout(Cout));
endmodule

module ripple_adder_8 (
  input  [7:0] A,
  input  [7:0] B,
  input  Cin,
  output [7:0] Y,
  output Cout,
  output C6
);

  wire full_adder_1_cout, full_adder_2_cout, full_adder_3_cout, full_adder_4_cout, full_adder_5_cout,
       full_adder_6_cout;

  full_adder full_adder_1 (.A(A[0]), .B(B[0]), .Cin(Cin), .Y(Y[0]), .Cout(full_adder_1_cout));
  full_adder full_adder_2 (.A(A[1]), .B(B[1]), .Cin(full_adder_1_cout), .Y(Y[1]), .Cout(full_adder_2_cout));
  full_adder full_adder_3 (.A(A[2]), .B(B[2]), .Cin(full_adder_2_cout), .Y(Y[2]), .Cout(full_adder_3_cout));
  full_adder full_adder_4 (.A(A[3]), .B(B[3]), .Cin(full_adder_3_cout), .Y(Y[3]), .Cout(full_adder_4_cout));
  full_adder full_adder_5 (.A(A[4]), .B(B[4]), .Cin(full_adder_4_cout), .Y(Y[4]), .Cout(full_adder_5_cout));
  full_adder full_adder_6 (.A(A[5]), .B(B[5]), .Cin(full_adder_5_cout), .Y(Y[5]), .Cout(full_adder_6_cout));
  full_adder full_adder_7 (.A(A[6]), .B(B[6]), .Cin(full_adder_6_cout), .Y(Y[6]), .Cout(C6));
  full_adder full_adder_8 (.A(A[7]), .B(B[7]), .Cin(C6), .Y(Y[7]), .Cout(Cout));
endmodule

module adder_subtractor (
  input  M,
  input  Cin,
  input  [7:0] B,
  input  [7:0] A,
  output [7:0] Y,
  output Cout,
  output Overflow
);

  wire ripple_adder_8_1_c6;
  wire [7:0] xor_8_out;

  xor xor_1 (xor_8_out[7], M, B[7]);
  xor xor_2 (xor_8_out[6], M, B[6]);
  xor xor_3 (xor_8_out[5], M, B[5]);
  xor xor_4 (xor_8_out[4], M, B[4]);
  xor xor_5 (xor_8_out[3], M, B[3]);
  xor xor_6 (xor_8_out[2], M, B[2]);
  xor xor_7 (xor_8_out[1], M, B[1]);
  xor xor_8 (xor_8_out[0], M, B[0]);
  ripple_adder_8 ripple_adder_8_1 (.A(A), .B(xor_8_out), .Cin(Cin), .Y(Y), .Cout(Cout), .C6(ripple_adder_8_1_c6));
  xor xor_9 (Overflow, Cout, ripple_adder_8_1_c6);
endmodule

module shifter_8 (
  input  [7:0] A,
  input  Cin,
  input  M,
  output [7:0] Y,
  output Cout
);

  mux_2to1 mux_2to1_1 (.IN0(A[2]), .IN1(A[4]), .S(M), .Y(Y[3]));
  mux_2to1 mux_2to1_2 (.IN0(A[6]), .IN1(Cin), .S(M), .Y(Y[7]));
  mux_2to1 mux_2to1_3 (.IN0(A[1]), .IN1(A[3]), .S(M), .Y(Y[2]));
  mux_2to1 mux_2to1_4 (.IN0(A[5]), .IN1(A[7]), .S(M), .Y(Y[6]));
  mux_2to1 mux_2to1_5 (.IN0(A[0]), .IN1(A[2]), .S(M), .Y(Y[1]));
  mux_2to1 mux_2to1_6 (.IN0(A[4]), .IN1(A[6]), .S(M), .Y(Y[5]));
  mux_2to1 mux_2to1_7 (.IN0(Cin), .IN1(A[1]), .S(M), .Y(Y[0]));
  mux_2to1 mux_2to1_8 (.IN0(A[3]), .IN1(A[5]), .S(M), .Y(Y[4]));
  mux_2to1 mux_2to1_9 (.IN0(A[7]), .IN1(A[0]), .S(M), .Y(Cout));
endmodule

module multiplier_4 (
  input  [3:0] B,
  input  [3:0] A,
  output [7:0] Y,
  output Overflow
);

  wire or_1_out, or_2_out;
  wire [2:0] and_2_out;
  wire [3:0] and_5_out, and_9_out, and_13_out;
  wire [3:1] ripple_adder_4_1_y, ripple_adder_4_2_y;
  wire [3:3] ripple_adder_4_1_cout, ripple_adder_4_2_cout;

  and and_1 (Y[0], A[0], B[0]);
  and and_2 (and_2_out[0], A[1], B[0]);
  and and_3 (and_2_out[1], A[2], B[0]);
  and and_4 (and_2_out[2], A[3], B[0]);
  and and_5 (and_5_out[0], A[0], B[1]);
  and and_6 (and_5_out[1], A[1], B[1]);
  and and_7 (and_5_out[2], A[2], B[1]);
  and and_8 (and_5_out[3], A[3], B[1]);
  ripple_adder_4 ripple_adder_4_1 (
    .A(and_5_out), .B({1'b0, and_2_out}), .Cin(1'b0), .Y({ripple_adder_4_1_y, Y[1]}),
    .Cout(ripple_adder_4_1_cout[3]));
  or or_1 (or_1_out, Y[4], Y[5]);
  or or_2 (or_2_out, or_1_out, Y[6]);
  or or_3 (Overflow, Y[7], or_2_out);
  and and_9 (and_9_out[0], A[0], B[2]);
  and and_10 (and_9_out[1], A[1], B[2]);
  and and_11 (and_9_out[2], A[2], B[2]);
  and and_12 (and_9_out[3], A[3], B[2]);
  ripple_adder_4 ripple_adder_4_2 (
    .A(and_9_out), .B({ripple_adder_4_1_cout[3], ripple_adder_4_1_y}), .Cin(1'b0),
    .Y({ripple_adder_4_2_y, Y[2]}), .Cout(ripple_adder_4_2_cout[3]));
  and and_13 (and_13_out[0], A[0], B[3]);
  ripple_adder_4 ripple_adder_4_3 (
    .A(and_13_out), .B({ripple_adder_4_2_cout[3], ripple_adder_4_2_y}), .Cin(1'b0), .Y(Y[6:3]), .Cout(Y[7]));
  and and_14 (and_13_out[1], A[1], B[3]);
  and and_15 (and_13_out[2], A[2], B[3]);
  and and_16 (and_13_out[3], A[3], B[3]);
endmodule

module alu (
  input  [7:0] A,
  input  [7:0] B,
  input  Cin,
  input  Vin,
  input  [3:0] OP,
  output [7:0] Y,
  output C,
  output V,
  output Z,
  output N,
  output HALT
);

  wire AdderC, AdderV, MulV, mux_8to1_1_out_10, mux_8to1_2_out_10, or_2_out, ShiftC;
  wire [7:0] AdderY, AndY, MulY, mux_8to1_8_1_out_10, OrY, ShiftY, XorY;

  adder_subtractor adder_subtractor_1 (
    .M(OP[0]), .B(B), .A(A), .Cin(Cin), .Y(AdderY), .Cout(AdderC), .Overflow(AdderV));
  multiplier_4 multiplier_4_1 (.B(B[3:0]), .A(A[3:0]), .Y(MulY), .Overflow(MulV));
  assign AndY = A & B;  // AND_Gate and_1, 8 bits wide
  assign OrY = A | B;  // OR_Gate or_1, 8 bits wide
  assign XorY = A ^ B;  // XOR_Gate xor_1, 8 bits wide
  shifter_8 shifter_8_1 (.A(A), .Cin(Cin), .M(OP[0]), .Y(ShiftY), .Cout(ShiftC));
  mux_8to1_8 mux_8to1_8_1 (
    .IN7(ShiftY), .IN6(ShiftY), .IN5(XorY), .IN4(OrY), .IN3(AndY), .IN2(MulY), .IN1(AdderY), .IN0(AdderY),
    .S(OP[2:0]), .out_10(mux_8to1_8_1_out_10));
  mux_8to1 mux_8to1_1 (
    .S(OP[2:0]), .I0(AdderC), .I1(AdderC), .I2(1'b0), .I3(Cin), .I4(Cin), .I5(Cin), .I6(ShiftC), .I7(ShiftC),
    .out_10(mux_8to1_1_out_10));
  mux_8to1 mux_8to1_2 (
    .S(OP[2:0]), .I0(AdderV), .I1(AdderV), .I2(MulV), .I3(Vin), .I4(Vin), .I5(Vin), .I6(Vin), .I7(Vin),
    .out_10(mux_8to1_2_out_10));
  mux_2to1_8 mux_2to1_8_1 (.S(OP[3]), .IN0(mux_8to1_8_1_out_10), .IN1(B), .Y({N, Y[6:0]}));
  mux_2to1 mux_2to1_1 (.IN0(mux_8to1_1_out_10), .IN1(Cin), .S(OP[3]), .Y(C));
  mux_2to1 mux_2to1_2 (.IN0(mux_8to1_2_out_10), .IN1(Cin), .S(OP[3]), .Y(V));
  nor nor_1 (Z, Y[0], Y[1], Y[2], Y[3], Y[4], Y[5], Y[6], N);
  or or_2 (or_2_out, OP[0], OP[1], OP[2]);
  and and_2 (HALT, or_2_out, OP[3]);

  assign Y[7] = N;

  // Other names for the same wires on the sheet: Mov[7:0] = B; OutC = C; OutV = V

  // Notes on the sheet:
  //   Execution =>
  //   Decoder =>
  //   HALT Signal generator
  //   <= Flags output
endmodule

module flag_mux (
  input  [7:0] CurFR,
  input  [3:0] NewFR,
  input  SelZ,
  input  SelN,
  input  SelC,
  input  SelV,
  output [7:0] FR
);

  mux_2to1 mux_2to1_1 (.IN0(CurFR[0]), .IN1(NewFR[0]), .S(SelZ), .Y(FR[0]));
  mux_2to1 mux_2to1_2 (.IN0(CurFR[1]), .IN1(NewFR[1]), .S(SelN), .Y(FR[1]));
  mux_2to1 mux_2to1_3 (.IN0(CurFR[2]), .IN1(NewFR[2]), .S(SelC), .Y(FR[2]));
  mux_2to1 mux_2to1_4 (.IN0(CurFR[3]), .IN1(NewFR[3]), .S(SelV), .Y(FR[3]));

  assign FR[7:4] = CurFR[7:4];
endmodule

module register_8 (
  input  CLK,
  input  WE,
  input  [7:0] D,
  output [7:0] Q
);

  wire d_flipflop_1_nq, d_flipflop_2_nq, d_flipflop_3_nq, d_flipflop_4_nq, d_flipflop_5_nq, d_flipflop_6_nq,
       d_flipflop_7_nq, mux_2to1_1_y, mux_2to1_2_y, mux_2to1_3_y, mux_2to1_4_y, mux_2to1_5_y, mux_2to1_6_y,
       mux_2to1_7_y, mux_2to1_8_y;

  mux_2to1 mux_2to1_1 (.IN0(Q[0]), .IN1(D[0]), .S(WE), .Y(mux_2to1_1_y));
  mux_2to1 mux_2to1_2 (.IN0(Q[1]), .IN1(D[1]), .S(WE), .Y(mux_2to1_2_y));
  mux_2to1 mux_2to1_3 (.IN0(Q[2]), .IN1(D[2]), .S(WE), .Y(mux_2to1_3_y));
  mux_2to1 mux_2to1_4 (.IN0(Q[3]), .IN1(D[3]), .S(WE), .Y(mux_2to1_4_y));
  mux_2to1 mux_2to1_5 (.IN0(Q[4]), .IN1(D[4]), .S(WE), .Y(mux_2to1_5_y));
  mux_2to1 mux_2to1_6 (.IN0(Q[5]), .IN1(D[5]), .S(WE), .Y(mux_2to1_6_y));
  mux_2to1 mux_2to1_7 (.IN0(Q[6]), .IN1(D[6]), .S(WE), .Y(mux_2to1_7_y));
  mux_2to1 mux_2to1_8 (.IN0(Q[7]), .IN1(D[7]), .S(WE), .Y(mux_2to1_8_y));
  d_flipflop d_flipflop_1 (.D(mux_2to1_1_y), .CLK(CLK), .Q(Q[0]), .NQ(d_flipflop_1_nq));
  // NoConnect on d_flipflop_1_nq
  d_flipflop d_flipflop_2 (.D(mux_2to1_2_y), .CLK(CLK), .Q(Q[1]), .NQ(d_flipflop_2_nq));
  // NoConnect on d_flipflop_2_nq
  d_flipflop d_flipflop_3 (.D(mux_2to1_3_y), .CLK(CLK), .Q(Q[2]), .NQ(d_flipflop_3_nq));
  // NoConnect on d_flipflop_3_nq
  d_flipflop d_flipflop_4 (.D(mux_2to1_4_y), .CLK(CLK), .Q(Q[3]), .NQ(d_flipflop_4_nq));
  // NoConnect on d_flipflop_4_nq
  d_flipflop d_flipflop_5 (.D(mux_2to1_5_y), .CLK(CLK), .Q(Q[4]), .NQ(d_flipflop_5_nq));
  // NoConnect on d_flipflop_5_nq
  d_flipflop d_flipflop_6 (.D(mux_2to1_6_y), .CLK(CLK), .Q(Q[5]), .NQ(d_flipflop_6_nq));
  // NoConnect on d_flipflop_6_nq
  d_flipflop d_flipflop_7 (.D(mux_2to1_7_y), .CLK(CLK), .Q(Q[6]), .NQ(d_flipflop_7_nq));
  // NoConnect on d_flipflop_7_nq
  d_flipflop d_flipflop_8 (.D(mux_2to1_8_y), .CLK(CLK), .Q(Q[7]));  // open: NQ
endmodule

module program_counter (
  input  CLK,
  input  Load,
  input  [15:0] PC,
  input  [15:0] D,
  output [15:0] NewPC
);

  wire adder_subtractor_1_cout, adder_subtractor_1_overflow, adder_subtractor_2_cout,
       adder_subtractor_2_overflow;
  wire [7:0] adder_subtractor_1_y, adder_subtractor_2_y, mux_2to1_8_1_y, mux_2to1_8_2_y;

  adder_subtractor adder_subtractor_1 (
    .M(1'b0), .B(D[7:0]), .A(PC[7:0]), .Cin(1'b0), .Y(adder_subtractor_1_y), .Cout(adder_subtractor_1_cout),
    .Overflow(adder_subtractor_1_overflow));
  // NoConnect on adder_subtractor_1_overflow
  adder_subtractor adder_subtractor_2 (
    .M(1'b0), .B(D[15:8]), .A(PC[15:8]), .Cin(adder_subtractor_1_cout), .Y(adder_subtractor_2_y),
    .Cout(adder_subtractor_2_cout), .Overflow(adder_subtractor_2_overflow));
  // NoConnect on adder_subtractor_2_overflow
  // NoConnect on adder_subtractor_2_cout
  mux_2to1_8 mux_2to1_8_1 (.S(Load), .IN0(adder_subtractor_1_y), .IN1(D[7:0]), .Y(mux_2to1_8_1_y));
  mux_2to1_8 mux_2to1_8_2 (.S(Load), .IN0(adder_subtractor_2_y), .IN1(D[15:8]), .Y(mux_2to1_8_2_y));
  register_8 LoPC (.CLK(CLK), .WE(1'b1), .D(mux_2to1_8_1_y), .Q(NewPC[7:0]));
  register_8 HiPC (.CLK(CLK), .WE(1'b1), .D({PC[15:12], mux_2to1_8_2_y[3:0]}), .Q(NewPC[15:8]));

  // Other names for the same wires on the sheet: HiPCNibble[3:0] = PC[15:12]; LoData[7:0] = D[7:0];
  //   HiData[7:0] = D[15:8]
endmodule

module instruction_decoder (
  input  [7:0] IR,
  input  [3:0] FR,
  output HLT,
  output [1:0] OP_TYPE,
  output FR_SELC,
  output FR_SELV,
  output FR_VAL,
  output MEM_WE,
  output MEM_RE,
  output WE_A,
  output WE_IX,
  output WE_IY,
  output MEM_IS_IND,
  output [1:0] MEM_SRC_SEL,
  output [1:0] REG_SEL,
  output [3:0] ALU_OP,
  output [1:0] OP_SEL,
  output UNY_CONST_FF,
  output UNY_CONST_C0
);

  wire and_1_out, ARI_HLT, ARI_WE_A, demux_2to1_1_y0, G_ARI, G_JMP, G_MEM, G_SYS, G_UNY, MEM_HLT, MEM_WE_A,
       MEM_WE_IX, MEM_WE_IY, or_1_out, or_2_out, SYS_HLT, UNY_HLT, UNY_WE_A, UNY_WE_IX, UNY_WE_IY;
  wire [1:0] ARI_OP_TYPE, MEM_OP_TYPE, MEM_REG_SEL, UNY_REG_SEL;
  wire [3:0] ARI_ALU_OP, UNY_ALU_OP;

  demux_2to1 demux_2to1_1 (.S(IR[7]), .I(1'b1), .Y0(demux_2to1_1_y0), .Y1(G_JMP));
  demux_4to1 demux_4to1_1 (.I(demux_2to1_1_y0), .S(IR[6:5]), .Y0(G_SYS), .Y1(G_MEM), .Y2(G_ARI), .Y3(G_UNY));
  decode_system decode_system_1 (
    .IR0(IR[0]), .IR1(IR[1]), .IR2(IR[2]), .IR3(IR[3]), .IR4(IR[4]), .E(G_SYS), .HLT(SYS_HLT),
    .SEL_C(FR_SELC), .SEL_V(FR_SELV), .VAL(FR_VAL));
  decode_memory decode_memory_1 (
    .IR0(IR[0]), .IR1(IR[1]), .IR2(IR[2]), .IR3(IR[3]), .IR4(IR[4]), .E(G_MEM), .HLT(MEM_HLT),
    .MEM_WE(MEM_WE), .MEM_RE(MEM_RE), .WE_A(MEM_WE_A), .WE_IX(MEM_WE_IX), .WE_IY(MEM_WE_IY),
    .IS_IND(MEM_IS_IND), .REG_SEL(MEM_REG_SEL), .SRC_SEL(MEM_SRC_SEL), .OP_TYPE(MEM_OP_TYPE));
  decode_arithmetic decode_arithmetic_1 (
    .IR0(IR[0]), .IR1(IR[1]), .IR2(IR[2]), .IR3(IR[3]), .IR4(IR[4]), .E(G_ARI), .HLT(ARI_HLT),
    .WE_A(ARI_WE_A), .ALU_OP(ARI_ALU_OP), .OP_SEL(OP_SEL), .OP_TYPE(ARI_OP_TYPE));
  decode_unary decode_unary_1 (
    .IR0(IR[0]), .IR1(IR[1]), .IR2(IR[2]), .IR3(IR[3]), .IR4(IR[4]), .E(G_UNY), .HLT(UNY_HLT),
    .CONST_FF(UNY_CONST_FF), .CONST_C0(UNY_CONST_C0), .WE_A(UNY_WE_A), .WE_IX(UNY_WE_IX), .WE_IY(UNY_WE_IY),
    .REG_SEL(UNY_REG_SEL), .ALU_OP(UNY_ALU_OP));
  or or_1 (or_1_out, IR[5], IR[6]);
  and and_1 (and_1_out, or_1_out, IR[7]);
  or or_2 (or_2_out, SYS_HLT, MEM_HLT, ARI_HLT, UNY_HLT);
  or or_3 (HLT, and_1_out, or_2_out);
  assign OP_TYPE = MEM_OP_TYPE | ARI_OP_TYPE;  // OR_Gate or_4, 2 bits wide
  or or_5 (WE_A, MEM_WE_A, ARI_WE_A, UNY_WE_A);
  or or_6 (WE_IX, MEM_WE_IX, UNY_WE_IX);
  or or_7 (WE_IY, MEM_WE_IY, UNY_WE_IY);
  assign REG_SEL = MEM_REG_SEL | UNY_REG_SEL;  // OR_Gate or_8, 2 bits wide
  assign ALU_OP = ARI_ALU_OP | UNY_ALU_OP;  // OR_Gate or_9, 4 bits wide

  // Other names for the same wires on the sheet: ARI_OP_SEL[1:0] = OP_SEL; OP_GROUP[2:0] = IR[7:5];
  //   SYS_SELC = FR_SELC; SYS_SELV = FR_SELV; SYS_VAL = FR_VAL

  // Notes on the sheet:
  //   Decode: Group
endmodule

module decode_system (
  input  IR0,
  input  IR1,
  input  IR2,
  input  IR3,
  input  IR4,
  input  E,
  output HLT,
  output SEL_C,
  output SEL_V,
  output VAL
);

  wire and_1_out, and_2_out, demux_2to1_1_y0, demux_2to1_1_y1, I_HLT, or_1_out, or_2_out;

  or or_1 (or_1_out, IR0, IR1);
  and and_1 (and_1_out, or_1_out, ~IR2);  // AND_Gate
  or or_2 (or_2_out, IR3, IR4);
  and and_2 (and_2_out, ~I_HLT, IR2);  // AND_Gate
  demux_2to1 demux_2to1_1 (.S(IR1), .I(and_2_out), .Y0(demux_2to1_1_y0), .Y1(demux_2to1_1_y1));
  and and_3 (HLT, E, I_HLT);
  or or_3 (I_HLT, and_1_out, or_2_out);
  and and_4 (SEL_C, E, demux_2to1_1_y0);
  and and_5 (SEL_V, demux_2to1_1_y1, E);
  and and_6 (VAL, IR0, E);

  // Other names for the same wires on the sheet: G_SYS = E
endmodule

module decode_memory (
  input  IR0,
  input  IR1,
  input  IR2,
  input  IR3,
  input  IR4,
  input  E,
  output HLT,
  output MEM_WE,
  output MEM_RE,
  output WE_A,
  output WE_IX,
  output WE_IY,
  output IS_IND,
  output [1:0] REG_SEL,
  output [1:0] SRC_SEL,
  output [1:0] OP_TYPE
);

  wire and_2_out, and_3_out, demux_4to1_1_y3, HLT_t, IS_IND_t, MEM_RE_t, MEM_WE_t, not_1_out, or_1_out,
       WE_A_t, WE_IX_t, WE_IY_t;
  wire [1:1] OP_TYPE_t;

  or or_1 (or_1_out, IR4, MEM_RE_t);
  not not_1 (not_1_out, IR4);
  not not_2 (OP_TYPE_t[1], IS_IND_t);
  demux_4to1 demux_4to1_1 (.I(or_1_out), .S({IR1, IR0}), .Y0(WE_A_t), .Y1(WE_IX_t), .Y2(WE_IY_t), .Y3(demux_4to1_1_y3));
  // NoConnect on demux_4to1_1_y3
  demux_2to1 demux_2to1_1 (.S(IR2), .I(not_1_out), .Y0(MEM_RE_t), .Y1(MEM_WE_t));
  and and_1 (IS_IND_t, IR3, not_1_out);
  and and_2 (and_2_out, IR0, IR1);
  or or_2 (HLT_t, and_2_out, and_3_out);
  and and_3 (and_3_out, IR2, IR3, IR4);
  and and_4 (HLT, E, HLT_t);
  and and_5 (MEM_WE, E, MEM_WE_t);
  and and_6 (MEM_RE, E, MEM_RE_t);
  and and_7 (WE_A, E, WE_A_t);
  and and_8 (WE_IX, E, WE_IX_t);
  and and_9 (WE_IY, E, WE_IY_t);
  and and_10 (IS_IND, E, IS_IND_t);
  assign REG_SEL = {2{E}} & {IR1, IR0};  // AND_Gate and_11, 2 bits wide
  assign SRC_SEL = {2{E}} & {IR3, IR2};  // AND_Gate and_12, 2 bits wide
  assign OP_TYPE = {2{E}} & {OP_TYPE_t[1], 1'b0};  // AND_Gate and_13, 2 bits wide

  // Other names for the same wires on the sheet: G_MEM = E; REG_SEL_t[1:0] = {IR1, IR0}; SRC_SEL_t[1:0] = {IR3, IR2}
endmodule

module decode_arithmetic (
  input  IR0,
  input  IR1,
  input  IR2,
  input  IR3,
  input  IR4,
  input  E,
  output HLT,
  output WE_A,
  output [3:0] ALU_OP,
  output [1:0] OP_SEL,
  output [1:0] OP_TYPE
);

  wire and_1_out, and_2_out, HLT_t, not_1_out, not_2_out, not_3_out, WE_A_t;
  wire [1:0] OP_TYPE_t;
  wire [2:0] ALU_OP_t;

  and and_1 (and_1_out, IR0, IR1, IR2);
  and and_2 (and_2_out, IR3, ~IR4);  // AND_Gate
  not not_1 (not_1_out, IR0);
  not not_2 (not_2_out, IR1);
  not not_3 (not_3_out, IR2);
  or or_1 (HLT_t, and_1_out, and_2_out);
  mux_2to1 mux_2to1_1 (.IN0(not_1_out), .IN1(IR0), .S(WE_A_t), .Y(ALU_OP_t[0]));
  mux_2to1 mux_2to1_2 (.IN0(not_2_out), .IN1(IR1), .S(WE_A_t), .Y(ALU_OP_t[1]));
  mux_2to1 mux_2to1_3 (.IN0(not_3_out), .IN1(IR2), .S(WE_A_t), .Y(ALU_OP_t[2]));
  nand nand_1 (WE_A_t, IR1, IR2);
  and and_3 (OP_TYPE_t[0], ~IR3, IR4);  // AND_Gate
  and and_4 (OP_TYPE_t[1], IR3, IR4);
  and and_5 (HLT, E, HLT_t);
  and and_6 (WE_A, E, WE_A_t);
  assign ALU_OP = {4{E}} & {1'b0, ALU_OP_t};  // AND_Gate and_7, 4 bits wide
  assign OP_SEL = {2{E}} & {IR4, IR3};  // AND_Gate and_8, 2 bits wide
  assign OP_TYPE = {2{E}} & OP_TYPE_t;  // AND_Gate and_9, 2 bits wide

  // Other names for the same wires on the sheet: G_ARI = E; OP_SEL_t[1:0] = {IR4, IR3}

  // Notes on the sheet:
  //   SIZE: 10xxxx->Byte/imm8; 11xxxx->Word/addr
endmodule

module decode_unary (
  input  IR0,
  input  IR1,
  input  IR2,
  input  IR3,
  input  IR4,
  input  E,
  output HLT,
  output CONST_FF,
  output CONST_C0,
  output WE_A,
  output WE_IX,
  output WE_IY,
  output [1:0] REG_SEL,
  output [3:0] ALU_OP
);

  wire CONST_C0_t, CONST_FF_t, demux_8to1_1_y2, demux_8to1_1_y3, demux_8to1_1_y4, HLT_t, I_DEC, I_INC, I_NOT,
       I_ROL, I_ROR, I_SHL, I_SHR, IS_HLT, not_1_out, or_2_out, or_3_out, REG_HLT, S_WE_A, U_WE_A, WE_A_t,
       WE_IX_t, WE_IY_t;
  wire [1:0] mux_2to1_1_y;
  wire [2:0] ALU_OP_t;

  not not_1 (not_1_out, IR3);
  demux_8to1 demux_8to1_1 (
    .I(not_1_out), .S({IR2, IR1, IR0}), .Y0(I_SHL), .Y1(I_SHR), .Y2(demux_8to1_1_y2), .Y3(demux_8to1_1_y3),
    .Y4(demux_8to1_1_y4), .Y5(I_NOT), .Y6(I_ROL), .Y7(I_ROR));
  and and_1 (S_WE_A, not_1_out, ~HLT_t);  // AND_Gate
  demux_2to1 demux_2to1_1 (.S(IR2), .I(IR3), .Y0(I_INC), .Y1(I_DEC));
  demux_4to1 demux_4to1_1 (.I(IR3), .S({IR1, IR0}), .Y0(U_WE_A), .Y1(WE_IX_t), .Y2(WE_IY_t), .Y3(REG_HLT));
  or or_1 (CONST_C0_t, I_SHL, I_SHR);
  or or_2 (or_2_out, I_SHR, I_ROR);
  or or_3 (or_3_out, I_SHL, I_ROL);
  or or_4 (CONST_FF_t, I_NOT, I_DEC);
  or or_5 (IS_HLT, demux_8to1_1_y2, demux_8to1_1_y3, demux_8to1_1_y4);
  or or_6 (ALU_OP_t[0], I_NOT, or_2_out);
  or or_7 (ALU_OP_t[1], or_2_out, or_3_out);
  or or_8 (ALU_OP_t[2], I_NOT, ALU_OP_t[1]);
  or or_9 (HLT_t, IR4, IS_HLT, REG_HLT);
  or or_10 (WE_A_t, S_WE_A, U_WE_A);
  mux_2to1 mux_2to1_1 (.IN0(IR0), .IN1(1'b0), .S(S_WE_A), .Y(mux_2to1_1_y[0]));
  mux_2to1 mux_2to1_2 (.IN0(IR1), .IN1(1'b0), .S(S_WE_A), .Y(mux_2to1_1_y[1]));
  and and_2 (HLT, E, HLT_t);
  and and_3 (CONST_FF, E, CONST_FF_t);
  and and_4 (CONST_C0, E, CONST_C0_t);
  and and_5 (WE_A, E, WE_A_t);
  and and_6 (WE_IX, E, WE_IX_t);
  and and_7 (WE_IY, E, WE_IY_t);
  assign REG_SEL = {2{E}} & mux_2to1_1_y;  // AND_Gate and_8, 2 bits wide
  assign ALU_OP = {4{E}} & {1'b0, ALU_OP_t};  // AND_Gate and_9, 4 bits wide

  // Other names for the same wires on the sheet: G_UNY = E; REG_SEL_t[1:0] = {IR1, IR0}

  // Notes on the sheet:
  //   OP[0]=W_SHR | W_SHL | W_NOT
  //   OP[1]=W_SHR | W_SHL | W_ROR | W_ROL
  //   OP[2]=W_SHR | W_SHL | W_ROR | W_ROL | W_NOT
endmodule
