// Logisim project ax8.circ as structural Verilog
module gpr_register_file (
  input  CLK,
  input  RST,
  input  [2:0] RDA_SEL,
  input  [2:0] RDB_SEL,
  input  WE,
  input  [2:0] WR_SEL,
  input  [1:0] WR_MODE,
  input  [15:0] WR_DATA,
  output [7:0] RDA_DATA,
  output [7:0] RDB_DATA,
  output [15:0] Z_DATA,
  output [15:0] SP_DATA
);

  wire adder_subtractor_8_1_cout, adder_subtractor_8_1_vout, adder_subtractor_8_2_cout,
       adder_subtractor_8_2_vout, DEC, demultiplexer_1_out1, INC, INC_CIN, IS_INC_DEC, or_3_out, or_4_out,
       or_5_out, or_6_out, WE_REG_A, WE_REG_B, WE_REG_C, WE_REG_D, WE_REG_H, WE_REG_L, WE_REG_SP, WE_REG_X,
       WE_REG_Y, WE_REG_Z, WR8, WR16;
  wire [7:0] adder_subtractor_8_2_y, HI_R16, LO_R16, multiplexer_3_out, multiplexer_4_out, multiplexer_5_out,
       multiplexer_6_out, REG_A_Q, REG_B_Q, REG_C_Q, REG_D_Q;

  Demultiplexer #(.select(2)) demultiplexer_1 (
    .out0(WR8), .out1(demultiplexer_1_out1), .out2(INC), .out3(DEC), .in(WE), .sel(WR_MODE));
  Demultiplexer #(.select(3)) demultiplexer_2 (
    .out0(WE_REG_A), .out1(WE_REG_B), .out2(WE_REG_C), .out3(WE_REG_D), .out4(WE_REG_X), .out5(WE_REG_Y),
    .out6(WE_REG_H), .out7(WE_REG_L), .in(WR8), .sel(WR_SEL));
  Demultiplexer demultiplexer_3 (.out0(WE_REG_Z), .out1(WE_REG_SP), .in(WR16), .sel(WR_SEL[0]));
  and and_1 (INC_CIN, INC, ~DEC);  // AND_Gate
  or or_1 (IS_INC_DEC, INC, DEC);
  or or_2 (WR16, demultiplexer_1_out1, INC, DEC);
  Multiplexer #(.select(3), .width(8)) multiplexer_1 (
    .in0(REG_A_Q), .in1(REG_B_Q), .in2(REG_C_Q), .in3(REG_D_Q), .in4(Z_DATA[7:0]), .in5(Z_DATA[15:8]),
    .in6(SP_DATA[15:8]), .in7(SP_DATA[7:0]), .out(RDA_DATA), .sel(RDA_SEL));
  Register reg_a (.D(WR_DATA[7:0]), .en(WE_REG_A), .clk(CLK), .Q(REG_A_Q), .clr(RST));
  Register reg_b (.D(WR_DATA[7:0]), .en(WE_REG_B), .clk(CLK), .Q(REG_B_Q), .clr(RST));
  Register reg_c (.D(WR_DATA[7:0]), .en(WE_REG_C), .clk(CLK), .Q(REG_C_Q), .clr(RST));
  Register reg_d (.D(WR_DATA[7:0]), .en(WE_REG_D), .clk(CLK), .Q(REG_D_Q), .clr(RST));
  Multiplexer #(.select(3), .width(8)) multiplexer_2 (
    .in0(REG_A_Q), .in1(REG_B_Q), .in2(REG_C_Q), .in3(REG_D_Q), .in4(Z_DATA[7:0]), .in5(Z_DATA[15:8]),
    .in6(SP_DATA[15:8]), .in7(SP_DATA[7:0]), .out(RDB_DATA), .sel(RDB_SEL));
  or or_3 (or_3_out, WE_REG_X, WE_REG_Z);
  or or_4 (or_4_out, WE_REG_H, WE_REG_SP);
  Multiplexer #(.width(8)) multiplexer_3 (
    .in0(Z_DATA[7:0]), .in1(SP_DATA[7:0]), .out(multiplexer_3_out), .sel(WR_SEL[0]));
  Multiplexer #(.width(8)) multiplexer_4 (
    .in0(Z_DATA[15:8]), .in1(SP_DATA[15:8]), .out(multiplexer_4_out), .sel(WR_SEL[0]));
  Register reg_x (.D(LO_R16), .en(or_3_out), .clk(CLK), .Q(Z_DATA[7:0]), .clr(RST));
  Register reg_l (.D(LO_R16), .en(or_4_out), .clk(CLK), .Q(SP_DATA[7:0]), .clr(RST));
  Multiplexer #(.width(8)) multiplexer_5 (
    .in0(WR_DATA[7:0]), .in1(multiplexer_3_out), .out(multiplexer_5_out), .sel(IS_INC_DEC));
  Multiplexer #(.width(8)) multiplexer_6 (
    .in0(WR_DATA[15:8]), .in1(multiplexer_4_out), .out(multiplexer_6_out), .sel(IS_INC_DEC));
  or or_5 (or_5_out, WE_REG_Y, WE_REG_Z);
  or or_6 (or_6_out, WE_REG_L, WE_REG_SP);
  Register reg_y (.D(HI_R16), .en(or_5_out), .clk(CLK), .Q(Z_DATA[15:8]), .clr(RST));
  Register reg_h (.D(HI_R16), .en(or_6_out), .clk(CLK), .Q(SP_DATA[15:8]), .clr(RST));
  adder_subtractor_8 adder_subtractor_8_1 (
    .A(multiplexer_5_out), .B({8{1'b0}}), .Cin(INC_CIN), .Mode(DEC), .Y(LO_R16),
    .Cout(adder_subtractor_8_1_cout), .Vout(adder_subtractor_8_1_vout));
  // NoConnect on adder_subtractor_8_1_vout
  adder_subtractor_8 adder_subtractor_8_2 (
    .A(multiplexer_6_out), .B({8{1'b0}}), .Cin(adder_subtractor_8_1_cout), .Mode(DEC),
    .Y(adder_subtractor_8_2_y), .Cout(adder_subtractor_8_2_cout), .Vout(adder_subtractor_8_2_vout));
  // NoConnect on adder_subtractor_8_2_cout
  // NoConnect on adder_subtractor_8_2_vout
  Multiplexer #(.width(8)) multiplexer_7 (.in0(LO_R16), .in1(adder_subtractor_8_2_y), .out(HI_R16), .sel(WR16));

  // Other names for the same wires on the sheet: REG_L_Q[7:0] = SP_DATA[7:0]; REG_H_Q[7:0] = SP_DATA[15:8];
  //   WR_DATA_L[7:0] = WR_DATA[7:0]; WR_DATA_H[7:0] = WR_DATA[15:8]; REG_X_Q[7:0] = Z_DATA[7:0];
  //   REG_Y_Q[7:0] = Z_DATA[15:8]
endmodule

module alu_dispatcher (
  input  CLK,
  input  Cin,
  input  [4:0] EncodedOp,
  input  [7:0] A,
  input  [7:0] B,
  output [15:0] Y,
  output NF,
  output VF,
  output CF,
  output ZF,
  output DISCARD_Y,
  output IS_WIDE,
  output BUSY,
  output DIV_BY_ZERO
);

  wire FORCE_NF, FORCE_VF, FORCE_ZF, multiplexer_6_out, multiplexer_7_out, multiplexer_8_out, TEST_BIT, U_CF,
       U_CIN, U_FORCE_A, U_FORCE_B, U_NF, U_VF, U_ZF, V_BUSY, V_DIV_BY_ZERO, V_NF, V_VF, V_ZF;
  wire [1:0] U_B_SEL, U_CIN_SEL;
  wire [2:0] ALU_OP;
  wire [7:0] B_MASK, multiplexer_2_out, not_1_out, U_A, U_B, U_Y, V_Y_HI, V_Y_LO;

  PLA #(.in_width(5), .out_width(14), .\table ("00000 00000000000000 # ADC\n00001 00100000000000 # SBC\n00010 01000000000000 # AND\n00011 01100000000000 # OR\n00100 10000000000000 # XOR\n00101 10100000000000 # ROR\n00110 11000000000000 # ROL\n00111 11100000000000 # MOV\n01000 00001000000000 # ADD\n01001 00110000000000 # SUB\n01010 01000011000010 # BCLR\n01011 01100011100010 # BSET\n01100 10000010100000 # NOT\n01101 10101000000000 # LSR\n01110 11001000000000 # LSL\n01111 11100010000000 # CLR\n10000 00010010000000 # INC\n10001 00101010000000 # DEC\n1001x 01000000011100 # BIT\n101xx 10111000000000 # ASR\n1100x 00110000010000 # CMP\n1101x 00110100000000 # NEG\n11100 00000000000001 # MULU\n11101 00100000000001 # DIVU\n11110 01000000000001 # MULS\n11111 01100000000001 # DIVS")) pla_1 (
    .in(EncodedOp),
    .out({ALU_OP, U_CIN_SEL, U_FORCE_A, U_FORCE_B, U_B_SEL, DISCARD_Y, FORCE_NF, FORCE_VF, FORCE_ZF, IS_WIDE}));
  Multiplexer #(.select(2)) multiplexer_1 (.in0(Cin), .in1(1'b0), .in2(1'b1), .in3(A[7]), .out(U_CIN), .sel(U_CIN_SEL));
  assign U_A = A & ~{8{U_FORCE_A}};  // AND_Gate and_1, 8 bits wide
  Decoder #(.enable("false"), .select(3)) decoder_1 (
    .out0(B_MASK[0]), .out1(B_MASK[1]), .out2(B_MASK[2]), .out3(B_MASK[3]), .out4(B_MASK[4]),
    .out5(B_MASK[5]), .out6(B_MASK[6]), .out7(B_MASK[7]), .sel(B[2:0]));
  u_alu u_alu_1 (.OP(ALU_OP), .A(U_A), .B(U_B), .Cin(U_CIN), .Y(U_Y), .ZF(U_ZF), .CF(U_CF), .VF(U_VF), .NF(U_NF));
  v_alu v_alu_1 (
    .CLK(CLK), .EN(IS_WIDE), .OP(ALU_OP[0]), .IsSigned(ALU_OP[1]), .A(A), .B(B), .Y({V_Y_HI, V_Y_LO}),
    .ZF(V_ZF), .VF(V_VF), .NF(V_NF), .Busy(V_BUSY), .DivByZero(V_DIV_BY_ZERO));
  assign not_1_out = ~B_MASK;  // NOT_Gate not_1, 8 bits wide
  Multiplexer #(.select(2), .width(8)) multiplexer_2 (
    .in0({8{1'b0}}), .in1({8{1'b1}}), .in2(not_1_out), .in3(B_MASK), .out(multiplexer_2_out), .sel(U_B_SEL));
  Multiplexer #(.select(3)) multiplexer_3 (
    .in0(A[0]), .in1(A[1]), .in2(A[2]), .in3(A[3]), .in4(A[4]), .in5(A[5]), .in6(A[6]), .in7(A[7]),
    .out(TEST_BIT), .sel(B[2:0]));
  Multiplexer #(.width(8)) multiplexer_4 (.in0(B), .in1(multiplexer_2_out), .out(U_B), .sel(U_FORCE_B));
  Multiplexer #(.width(8)) multiplexer_5 (.in0(U_Y), .in1(V_Y_LO), .out(Y[7:0]), .sel(IS_WIDE));
  assign Y[15:8] = {8{IS_WIDE}} & V_Y_HI;  // AND_Gate and_2, 8 bits wide
  Multiplexer multiplexer_6 (.in0(U_ZF), .in1(V_ZF), .out(multiplexer_6_out), .sel(IS_WIDE));
  Multiplexer multiplexer_7 (.in0(U_VF), .in1(V_VF), .out(multiplexer_7_out), .sel(IS_WIDE));
  Multiplexer multiplexer_8 (.in0(U_NF), .in1(V_NF), .out(multiplexer_8_out), .sel(IS_WIDE));
  Multiplexer multiplexer_9 (.in0(multiplexer_6_out), .in1(TEST_BIT), .out(ZF), .sel(FORCE_ZF));
  Multiplexer multiplexer_10 (.in0(multiplexer_7_out), .in1(B[6]), .out(VF), .sel(FORCE_VF));
  Multiplexer multiplexer_11 (.in0(multiplexer_8_out), .in1(B[7]), .out(NF), .sel(FORCE_NF));
  and and_3 (CF, U_CF, ~IS_WIDE);  // AND_Gate
  and and_4 (BUSY, IS_WIDE, V_BUSY);
  and and_5 (DIV_BY_ZERO, IS_WIDE, V_DIV_BY_ZERO);

  // Other names for the same wires on the sheet: U_OP[2:0] = ALU_OP; V_OP = ALU_OP[0]; V_IS_SIGNED = ALU_OP[1];
  //   ALU_SEL = IS_WIDE; EOP[4:0] = EncodedOp; IN_A[7:0] = A; B_MASK_SEL[2:0] = B[2:0]; IN_B[7:0] = B; OUT_NF = NF;
  //   OUT_VF = VF; OUT_ZF = ZF; OUT_Y_LO[7:0] = Y[7:0]; OUT_Y_HI[7:0] = Y[15:8]
endmodule

module u_alu (
  input  [2:0] OP,
  input  [7:0] A,
  input  [7:0] B,
  input  Cin,
  output [7:0] Y,
  output ZF,
  output CF,
  output VF,
  output NF
);

  wire ADC_SBC_COUT, ADC_SBC_VOUT, and_2_out, and_3_out, ROT_COUT, xor_2_out;
  wire [7:0] ADC_SBC_Y, AND_Y, OR_Y, ROT_Y, XOR_Y;

  assign AND_Y = A & B;  // AND_Gate and_1, 8 bits wide
  assign OR_Y = A | B;  // OR_Gate or_1, 8 bits wide
  assign XOR_Y = A ^ B;  // XOR_Gate xor_1, 8 bits wide
  adder_subtractor_8 adder_subtractor_8_1 (
    .A(A), .B(B), .Cin(Cin), .Mode(OP[0]), .Y(ADC_SBC_Y), .Cout(ADC_SBC_COUT), .Vout(ADC_SBC_VOUT));
  shift_rotator_8 shift_rotator_8_1 (.A(A), .Cin(Cin), .Dir(OP[0]), .Y(ROT_Y), .COUT(ROT_COUT));
  xor xor_2 (xor_2_out, OP[0], OP[1]);
  and and_2 (and_2_out, ADC_SBC_COUT, ~OP[1], ~OP[2]);  // AND_Gate
  and and_3 (and_3_out, ROT_COUT, xor_2_out, OP[2]);
  Multiplexer #(.select(3), .width(8)) multiplexer_1 (
    .in0(ADC_SBC_Y), .in1(ADC_SBC_Y), .in2(AND_Y), .in3(OR_Y), .in4(XOR_Y), .in5(ROT_Y), .in6(ROT_Y),
    .in7(B), .out({NF, Y[6:0]}), .sel(OP));
  nor nor_1 (ZF, Y[0], Y[1], Y[2], Y[3], Y[4], Y[5], Y[6], NF, NF);
  or or_2 (CF, and_2_out, and_3_out);
  and and_4 (VF, ADC_SBC_VOUT, ~OP[1], ~OP[2]);  // AND_Gate

  assign Y[7] = NF;

  // Other names for the same wires on the sheet: IN_A[7:0] = A; IN_B[7:0] = B; IN_OP[2:0] = OP;
  //   Y_OUT[7:0] = {NF, Y[6:0]}
endmodule

module v_alu (
  input  CLK,
  input  EN,
  input  OP,
  input  IsSigned,
  input  [7:0] A,
  input  [7:0] B,
  output [15:0] Y,
  output ZF,
  output VF,
  output NF,
  output Busy,
  output DivByZero
);

  wire A_SIGN, ABORT, adder_subtractor_8_1_cout, and_6_out, B_SIGN, C0, C1, C2, IS_SIGNED, nor_1_out,
       nor_2_out, RST, sign_bridge_8_1_chainout, sign_bridge_8_2_chainout, sign_bridge_8_3_chainout,
       sign_bridge_8_4_chainout, T0, T1, T2, T3, xor_1_out, xor_2_out, xor_3_out, xor_4_out;
  wire [7:0] A_Q, A_t, B_Q, B_t, DIV_OUT_A, DIV_OUT_B, MUL_OUT_A, MUL_OUT_B, multiplexer_1_out,
       multiplexer_2_out, NEXT_A, NEXT_B, PRE_OUT_Y_HI, PRE_OUT_Y_LO, sign_bridge_8_3_y, sign_bridge_8_4_y;
  wire [15:0] DIV_Y, MUL_Y;

  and and_1 (C0, Busy, T0);
  and and_2 (C1, T1, C0);
  and and_3 (C2, T2, C1);
  and and_4 (A_SIGN, A[7], IsSigned);
  and and_5 (B_SIGN, B[7], IsSigned);
  not not_1 (RST, EN);
  D_Flip_Flop d_ff_1 (.D(nor_1_out), .clk(CLK), .Q(Busy), .preset(RST));  // open: Qn, reset
  nor nor_1 (nor_1_out, T3, ABORT);
  D_Flip_Flop d_ff_2 (.D(xor_1_out), .clk(CLK), .Q(T0), .reset(RST));  // open: Qn, preset
  xor xor_1 (xor_1_out, Busy, T0);
  D_Flip_Flop d_ff_3 (.D(xor_2_out), .clk(CLK), .Q(T1), .reset(RST));  // open: Qn, preset
  xor xor_2 (xor_2_out, T1, C0);
  D_Flip_Flop d_ff_4 (.D(xor_3_out), .clk(CLK), .Q(T2), .reset(RST));  // open: Qn, preset
  xor xor_3 (xor_3_out, T2, C1);
  D_Flip_Flop d_ff_5 (.D(xor_4_out), .clk(CLK), .Q(T3), .reset(RST));  // open: Qn, preset
  xor xor_4 (xor_4_out, T3, C2);
  xor xor_5 (IS_SIGNED, A_SIGN, B_SIGN);
  Multiplexer #(.width(8)) multiplexer_1 (.in0(A_t), .in1(NEXT_A), .out(multiplexer_1_out), .sel(Busy));
  Multiplexer #(.width(8)) multiplexer_2 (.in0(B_t), .in1(NEXT_B), .out(multiplexer_2_out), .sel(Busy));
  Register A_BUF (.D(multiplexer_1_out), .en(1'b1), .clk(CLK), .Q(A_Q), .clr(RST));
  Register B_BUF (.D(multiplexer_2_out), .en(1'b1), .clk(CLK), .Q(B_Q), .clr(RST));
  sign_bridge_8 sign_bridge_8_1 (.A(A), .ChainIn(1'b1), .Sign(A_SIGN), .Y(A_t), .ChainOut(sign_bridge_8_1_chainout));
  // NoConnect on sign_bridge_8_1_chainout
  sign_bridge_8 sign_bridge_8_2 (.A(B), .ChainIn(1'b1), .Sign(B_SIGN), .Y(B_t), .ChainOut(sign_bridge_8_2_chainout));
  // NoConnect on sign_bridge_8_2_chainout
  nor nor_2 (nor_2_out, B[0], B[1], B[2], B[3], B[4], B[5], B[6], B[7], B[7]);
  and and_6 (and_6_out, Busy, CLK);
  and and_7 (DivByZero, nor_2_out, OP);
  adder_subtractor_8 adder_subtractor_8_1 (
    .A(A_t), .B(B_t), .Cin(1'b1), .Mode(1'b1), .Cout(adder_subtractor_8_1_cout));  // open: Y, Vout
  and and_8 (VF, OP, ~adder_subtractor_8_1_cout);  // AND_Gate
  or or_1 (ABORT, DivByZero, VF);
  sign_bridge_8 sign_bridge_8_3 (
    .A(PRE_OUT_Y_LO), .ChainIn(1'b1), .Sign(IS_SIGNED), .Y(sign_bridge_8_3_y),
    .ChainOut(sign_bridge_8_3_chainout));
  sign_bridge_8 sign_bridge_8_4 (
    .A(PRE_OUT_Y_HI), .ChainIn(sign_bridge_8_3_chainout), .Sign(IS_SIGNED), .Y(sign_bridge_8_4_y),
    .ChainOut(sign_bridge_8_4_chainout));
  // NoConnect on sign_bridge_8_4_chainout
  multiplier_8 multiplier_8_1 (
    .CLK(and_6_out), .RST(RST), .InM(A_Q), .InQ(B_Q), .Y(MUL_Y), .OutM(MUL_OUT_A), .OutQ(MUL_OUT_B));
  divisor_8 divisor_8_1 (
    .CLK(and_6_out), .RST(RST), .InQ(A_Q), .InM(B_Q), .Done(T3), .Y(DIV_Y), .OutQ(DIV_OUT_A), .OutM(DIV_OUT_B));
  Multiplexer #(.width(8)) multiplexer_3 (.in0(sign_bridge_8_3_y), .in1({8{1'b0}}), .out(Y[7:0]), .sel(ABORT));
  Multiplexer #(.width(8)) multiplexer_4 (.in0(sign_bridge_8_4_y), .in1(A), .out({NF, Y[14:8]}), .sel(ABORT));
  nor nor_3 (ZF, Y[0], Y[1], Y[2], Y[3], Y[4], Y[5], Y[6], Y[7], Y[8], Y[9], Y[10], Y[11], Y[12], Y[13], Y[14], NF);
  Multiplexer #(.width(16)) multiplexer_5 (.in0(MUL_Y), .in1(DIV_Y), .out({PRE_OUT_Y_HI, PRE_OUT_Y_LO}), .sel(OP));
  Multiplexer #(.width(8)) multiplexer_6 (.in0(MUL_OUT_A), .in1(DIV_OUT_A), .out(NEXT_A), .sel(OP));
  Multiplexer #(.width(8)) multiplexer_7 (.in0(MUL_OUT_B), .in1(DIV_OUT_B), .out(NEXT_B), .sel(OP));

  assign Y[15] = NF;

  // Other names for the same wires on the sheet: DIV_BY_ZERO = DivByZero; IN_A[7:0] = A; IN_B[7:0] = B; IS_DIV = OP;
  //   SIGN = IsSigned; OUT_Y_LO[7:0] = Y[7:0]; OUT_Y_HI[7:0] = {NF, Y[14:8]}

  // Notes on the sheet:
  //   STATE MACHINE =>
  //   PRE SIGN CORRECTION
  //   Check for edge cases in division
  //   POST SIGN CORRECTION
endmodule

module multiplier_8 (
  input  CLK,
  input  RST,
  input  [7:0] InM,
  input  [7:0] InQ,
  output [15:0] Y,
  output [7:0] OutM,
  output [7:0] OutQ
);

  wire adder_subtractor_8_1_cout, adder_subtractor_8_1_vout, adder_subtractor_8_2_cout,
       adder_subtractor_8_2_vout, shift_rotator_8_1_cout, shift_rotator_8_2_cout, shift_rotator_8_3_cout;
  wire [7:0] HI_Q, NEXT_HI_ACC, NEXT_HI_Q, NEXT_LO_ACC;

  Register register_1 (.D(NEXT_LO_ACC), .en(InM[0]), .clk(CLK), .Q(Y[7:0]), .clr(RST));
  Register register_2 (.D(NEXT_HI_ACC), .en(InM[0]), .clk(CLK), .Q(Y[15:8]), .clr(RST));
  Register register_3 (.D(NEXT_HI_Q), .en(1'b1), .clk(CLK), .Q(HI_Q), .clr(RST));
  adder_subtractor_8 adder_subtractor_8_1 (
    .A(Y[7:0]), .B(InQ), .Cin(1'b0), .Mode(1'b0), .Y(NEXT_LO_ACC), .Cout(adder_subtractor_8_1_cout),
    .Vout(adder_subtractor_8_1_vout));
  // NoConnect on adder_subtractor_8_1_vout
  adder_subtractor_8 adder_subtractor_8_2 (
    .A(Y[15:8]), .B(HI_Q), .Cin(adder_subtractor_8_1_cout), .Mode(1'b0), .Y(NEXT_HI_ACC),
    .Cout(adder_subtractor_8_2_cout), .Vout(adder_subtractor_8_2_vout));
  // NoConnect on adder_subtractor_8_2_cout
  // NoConnect on adder_subtractor_8_2_vout
  shift_rotator_8 shift_rotator_8_1 (.A(InM), .Cin(1'b0), .Dir(1'b0), .Y(OutM), .COUT(shift_rotator_8_1_cout));
  // NoConnect on shift_rotator_8_1_cout
  shift_rotator_8 shift_rotator_8_2 (.A(InQ), .Cin(1'b0), .Dir(1'b1), .Y(OutQ), .COUT(shift_rotator_8_2_cout));
  shift_rotator_8 shift_rotator_8_3 (
    .A(HI_Q), .Cin(shift_rotator_8_2_cout), .Dir(1'b1), .Y(NEXT_HI_Q), .COUT(shift_rotator_8_3_cout));
  // NoConnect on shift_rotator_8_3_cout

  // Other names for the same wires on the sheet: IN_M[7:0] = InM; M_LSB = InM[0]; LO_Q[7:0] = InQ; OUT_M[7:0] = OutM;
  //   OUT_Q[7:0] = OutQ; LO_ACC[7:0] = Y[7:0]; HI_ACC[7:0] = Y[15:8]
endmodule

module divisor_8 (
  input  CLK,
  input  RST,
  input  [7:0] InQ,
  input  [7:0] InM,
  input  Done,
  output [15:0] Y,
  output [7:0] OutQ,
  output [7:0] OutM
);

  wire ACC_IS_NEG, ACC_LSB, adder_subtractor_8_1_cout, adder_subtractor_8_1_vout, and_2_out, N_DONE, OP_CTRL,
       shift_rotator_8_1_cout;
  wire [0:0] SHL_Q;
  wire [7:0] MATH_IN_ACC, MATH_OUT_ACC, SHL_ACC;
  wire [7:1] ACC_Q;

  Register register_1 (.D(MATH_OUT_ACC), .en(N_DONE), .clk(CLK), .Q({ACC_Q, ACC_LSB}), .clr(RST));
  not not_1 (N_DONE, Done);
  shift_rotator_8 shift_rotator_8_1 (
    .A(InQ), .Cin(1'b0), .Dir(1'b1), .Y({OutQ[7:1], SHL_Q[0]}), .COUT(shift_rotator_8_1_cout));
  shift_rotator_8 shift_rotator_8_2 (
    .A({ACC_Q, ACC_LSB}), .Cin(shift_rotator_8_1_cout), .Dir(1'b1), .Y(SHL_ACC), .COUT(ACC_IS_NEG));
  adder_subtractor_8 adder_subtractor_8_1 (
    .A(MATH_IN_ACC), .B(InM), .Cin(OP_CTRL), .Mode(OP_CTRL), .Y(MATH_OUT_ACC),
    .Cout(adder_subtractor_8_1_cout), .Vout(adder_subtractor_8_1_vout));
  // NoConnect on adder_subtractor_8_1_cout
  // NoConnect on adder_subtractor_8_1_vout
  and and_1 (OP_CTRL, N_DONE, ~ACC_IS_NEG);  // AND_Gate
  Multiplexer #(.width(8)) multiplexer_1 (.in0({ACC_Q, ACC_LSB}), .in1(SHL_ACC), .out(MATH_IN_ACC), .sel(N_DONE));
  and and_2 (and_2_out, ACC_IS_NEG, Done);
  Multiplexer #(.width(8)) multiplexer_2 (.in0({ACC_Q, ACC_LSB}), .in1(MATH_OUT_ACC), .out(Y[15:8]), .sel(and_2_out));
  not not_2 (OutQ[0], MATH_OUT_ACC[7]);

  assign OutM = InM;
  assign Y[7:0] = InQ;

  // Other names for the same wires on the sheet: ACC_Q[0] = ACC_LSB; IN_M[7:0] = InM; Q_BIT = MATH_OUT_ACC[7];
  //   SHL_Q[7:1] = OutQ[7:1]; IN_Q[7:0] = InQ; OUT_ACC[7:0] = Y[15:8]
endmodule

module adder_subtractor_8 (
  input  [7:0] A,
  input  [7:0] B,
  input  Cin,
  input  Mode,
  output [7:0] Y,
  output Cout,
  output Vout
);

  wire B0, B1, B2, B3, B4, B5, B6, B7, full_adder_1_cout, full_adder_2_cout, full_adder_3_cout,
       full_adder_4_cout, full_adder_5_cout, full_adder_6_cout, full_adder_7_cout;

  assign {B7, B6, B5, B4, B3, B2, B1, B0} = B ^ {8{Mode}};  // XOR_Gate xor_1, 8 bits wide
  full_adder full_adder_1 (.A(A[0]), .B(B0), .Cin(Cin), .Y(Y[0]), .Cout(full_adder_1_cout));
  full_adder full_adder_2 (.A(A[1]), .B(B1), .Cin(full_adder_1_cout), .Y(Y[1]), .Cout(full_adder_2_cout));
  full_adder full_adder_3 (.A(A[2]), .B(B2), .Cin(full_adder_2_cout), .Y(Y[2]), .Cout(full_adder_3_cout));
  full_adder full_adder_4 (.A(A[3]), .B(B3), .Cin(full_adder_3_cout), .Y(Y[3]), .Cout(full_adder_4_cout));
  full_adder full_adder_5 (.A(A[4]), .B(B4), .Cin(full_adder_4_cout), .Y(Y[4]), .Cout(full_adder_5_cout));
  full_adder full_adder_6 (.A(A[5]), .B(B5), .Cin(full_adder_5_cout), .Y(Y[5]), .Cout(full_adder_6_cout));
  full_adder full_adder_7 (.A(A[6]), .B(B6), .Cin(full_adder_6_cout), .Y(Y[6]), .Cout(full_adder_7_cout));
  full_adder full_adder_8 (.A(A[7]), .B(B7), .Cin(full_adder_7_cout), .Y(Y[7]), .Cout(Cout));
  xor xor_2 (Vout, full_adder_7_cout, Cout);
endmodule

module full_adder (
  input  A,
  input  B,
  input  Cin,
  output Y,
  output Cout
);

  wire and_1_out, and_2_out, xor_1_out;

  xor xor_1 (xor_1_out, A, B);
  and and_1 (and_1_out, xor_1_out, Cin);
  and and_2 (and_2_out, A, B);
  xor xor_2 (Y, xor_1_out, Cin);
  or or_1 (Cout, and_1_out, and_2_out);
endmodule

module shift_rotator_8 (
  input  [7:0] A,
  input  Cin,
  input  Dir,
  output [7:0] Y,
  output COUT
);

  Multiplexer multiplexer_1 (.in0(A[1]), .in1(Cin), .out(Y[0]), .sel(Dir));
  Multiplexer multiplexer_2 (.in0(A[5]), .in1(A[3]), .out(Y[4]), .sel(Dir));
  Multiplexer multiplexer_3 (.in0(A[0]), .in1(A[7]), .out(COUT), .sel(Dir));
  Multiplexer multiplexer_4 (.in0(A[2]), .in1(A[0]), .out(Y[1]), .sel(Dir));
  Multiplexer multiplexer_5 (.in0(A[3]), .in1(A[1]), .out(Y[2]), .sel(Dir));
  Multiplexer multiplexer_6 (.in0(A[6]), .in1(A[4]), .out(Y[5]), .sel(Dir));
  Multiplexer multiplexer_7 (.in0(A[7]), .in1(A[5]), .out(Y[6]), .sel(Dir));
  Multiplexer multiplexer_8 (.in0(A[4]), .in1(A[2]), .out(Y[3]), .sel(Dir));
  Multiplexer multiplexer_9 (.in0(Cin), .in1(A[6]), .out(Y[7]), .sel(Dir));
endmodule

module sign_bridge_8 (
  input  [7:0] A,
  input  ChainIn,
  input  Sign,
  output [7:0] Y,
  output ChainOut
);

  wire and_1_out, and_2_out, and_3_out, and_4_out, and_5_out, and_6_out, and_7_out, and_8_out, N_CIN,
       or_1_out, or_2_out, or_3_out, or_4_out, or_5_out, or_6_out, or_7_out, or_8_out;

  not not_1 (N_CIN, ChainIn);
  or or_1 (or_1_out, A[0], N_CIN);
  or or_2 (or_2_out, A[0], N_CIN, A[1]);
  or or_3 (or_3_out, or_2_out, N_CIN, A[2]);
  or or_4 (or_4_out, or_3_out, N_CIN, A[3]);
  or or_5 (or_5_out, or_4_out, N_CIN, A[4]);
  or or_6 (or_6_out, or_5_out, N_CIN, A[5]);
  or or_7 (or_7_out, or_6_out, N_CIN, A[6]);
  or or_8 (or_8_out, or_7_out, A[7]);
  and and_1 (and_1_out, N_CIN, Sign);
  and and_2 (and_2_out, or_1_out, Sign);
  and and_3 (and_3_out, or_2_out, Sign);
  and and_4 (and_4_out, or_3_out, Sign);
  and and_5 (and_5_out, or_4_out, Sign);
  and and_6 (and_6_out, or_5_out, Sign);
  and and_7 (and_7_out, or_6_out, Sign);
  and and_8 (and_8_out, or_7_out, Sign);
  and and_9 (ChainOut, or_8_out, N_CIN);
  xor xor_1 (Y[0], A[0], and_1_out);
  xor xor_2 (Y[1], A[1], and_2_out);
  xor xor_3 (Y[2], A[2], and_3_out);
  xor xor_4 (Y[3], A[3], and_4_out);
  xor xor_5 (Y[4], A[4], and_5_out);
  xor xor_6 (Y[5], A[5], and_6_out);
  xor xor_7 (Y[6], A[6], and_7_out);
  xor xor_8 (Y[7], A[7], and_8_out);

  // Other names for the same wires on the sheet: COUT = ChainOut

  // Notes on the sheet:
  //   Only convert if in chained mode. 
  //   Keep chain if all bit were zero in this byte
endmodule
